// Logisim project StopWatch.circ as structural Verilog
module \数码管驱动  (
  input  X3,
  input  X2,
  input  X1,
  input  X0,
  output Seg_1,
  output Seg_2,
  output Seg_3,
  output Seg_4,
  output Seg_5,
  output Seg_6,
  output Seg_7
);

  wire and_1_out, and_2_out, and_3_out, and_4_out, and_5_out, and_6_out, and_7_out, and_8_out, and_9_out,
       and_10_out, and_11_out, and_12_out, and_13_out, and_14_out, and_15_out, and_16_out, and_17_out,
       and_18_out, and_19_out, not_1_out, not_2_out, not_3_out, not_4_out, not_5_out, not_6_out, not_7_out,
       not_8_out, not_9_out, not_10_out, not_11_out, not_12_out, not_13_out, not_14_out, not_15_out,
       not_16_out, not_17_out, not_18_out, not_19_out, not_20_out, not_21_out, not_22_out, not_23_out,
       not_24_out, not_25_out, not_26_out, not_27_out, not_28_out;

  not not_1 (not_1_out, X2);
  and and_1 (and_1_out, not_1_out, X1);
  and and_2 (and_2_out, X2, not_2_out);
  not not_2 (not_2_out, X1);
  and and_3 (and_3_out, X2, not_3_out);
  not not_3 (not_3_out, X0);
  not not_4 (not_4_out, X1);
  and and_4 (and_4_out, not_4_out, not_5_out);
  not not_5 (not_5_out, X0);
  and and_5 (and_5_out, X2, not_6_out);
  not not_6 (not_6_out, X1);
  and and_6 (and_6_out, X2, not_7_out);
  not not_7 (not_7_out, X0);
  not not_8 (not_8_out, X2);
  and and_7 (and_7_out, not_8_out, not_9_out);
  not not_9 (not_9_out, X0);
  and and_8 (and_8_out, X2, X0);
  not not_10 (not_10_out, X3);
  and and_9 (and_9_out, not_10_out, not_11_out);
  not not_11 (not_11_out, X2);
  not not_12 (not_12_out, X2);
  and and_10 (and_10_out, not_12_out, not_13_out);
  not not_13 (not_13_out, X1);
  not not_14 (not_14_out, X1);
  and and_11 (and_11_out, not_14_out, not_15_out);
  not not_15 (not_15_out, X0);
  and and_12 (and_12_out, X1, X0);
  not not_16 (not_16_out, X3);
  and and_13 (and_13_out, not_16_out, not_17_out, not_18_out);
  not not_17 (not_17_out, X2);
  not not_18 (not_18_out, X0);
  not not_19 (not_19_out, X2);
  and and_14 (and_14_out, not_19_out, not_20_out, not_21_out);
  not not_20 (not_20_out, X1);
  not not_21 (not_21_out, X0);
  and and_15 (and_15_out, X2, X1, not_22_out);
  not not_22 (not_22_out, X0);
  not not_23 (not_23_out, X2);
  and and_16 (and_16_out, not_23_out, not_24_out);
  not not_24 (not_24_out, X0);
  not not_25 (not_25_out, X2);
  and and_17 (and_17_out, not_25_out, X1);
  and and_18 (and_18_out, X1, not_26_out);
  not not_26 (not_26_out, X0);
  and and_19 (and_19_out, X2, not_27_out, X0);
  not not_27 (not_27_out, X1);
  not not_28 (not_28_out, X1);
  or or_1 (Seg_7, not_28_out, X0, X2);
  or or_2 (Seg_1, and_1_out, and_2_out, and_3_out, X3);
  or or_3 (Seg_2, and_4_out, and_5_out, and_6_out, X3);
  or or_4 (Seg_3, and_7_out, X1, and_8_out, X3);
  or or_5 (Seg_4, and_9_out, and_10_out, and_11_out, and_12_out);
  or or_6 (Seg_5, and_13_out, and_14_out, and_15_out);
  or or_7 (Seg_6, and_16_out, and_17_out, and_18_out, and_19_out, X3);
endmodule

module \数码管驱动测试  (
);

  wire clock_1_out, \数码管驱动_1_seg_1 , \数码管驱动_1_seg_2 , \数码管驱动_1_seg_3 , \数码管驱动_1_seg_4 , \数码管驱动_1_seg_5 ,
       \数码管驱动_1_seg_6 , \数码管驱动_1_seg_7 ;
  wire [3:0] counter_1_q;

  Counter #(.width(4), .max('hf)) counter_1 (.Q(counter_1_q), .clk(clock_1_out));  // open: load, D, count, carry, clr
  Clock clock_1 (.out(clock_1_out));
  \数码管驱动  \u_数码管驱动_1  (
    .X3(counter_1_q[3]), .X2(counter_1_q[2]), .Seg_1(\数码管驱动_1_seg_1 ), .X1(counter_1_q[1]),
    .X0(counter_1_q[0]), .Seg_2(\数码管驱动_1_seg_2 ), .Seg_3(\数码管驱动_1_seg_3 ), .Seg_4(\数码管驱动_1_seg_4 ),
    .Seg_5(\数码管驱动_1_seg_5 ), .Seg_6(\数码管驱动_1_seg_6 ), .Seg_7(\数码管驱动_1_seg_7 ));
  _7_Segment_Display u_7_segment_display_1 (
    .g(\数码管驱动_1_seg_1 ), .f(\数码管驱动_1_seg_2 ), .a(\数码管驱动_1_seg_3 ), .b(\数码管驱动_1_seg_4 ), .e(\数码管驱动_1_seg_5 ),
    .d(\数码管驱动_1_seg_6 ), .c(\数码管驱动_1_seg_7 ));  // open: dp

  // Notes on the sheet:
  //   Ctrl+T驱动时钟单步运行测试
endmodule

// MUX
module \_2路选择器_1位  (
  input  X0,
  input  Sel,
  input  X1,
  output Out
);

  wire and_1_out, and_2_out, not_1_out;

  not not_1 (not_1_out, X1);
  and and_1 (and_1_out, Sel, X1);
  and and_2 (and_2_out, X0, not_1_out);
  or or_1 (Out, and_1_out, and_2_out);
endmodule

// MUX
module \_2路选择器_16位  (
  input  [15:0] X,
  input  [15:0] Y,
  input  Sel,
  output [15:0] Out
);

  // Probe on X
  // Probe on Y
  // Probe on Sel
  \_2路选择器_1位  \u_2路选择器_1位_1  (.X0(X[0]), .Out(Out[0]), .Sel(Y[0]), .X1(Sel));
  \_2路选择器_1位  \u_2路选择器_1位_2  (.X0(X[8]), .Out(Out[8]), .Sel(Y[8]), .X1(Sel));
  \_2路选择器_1位  \u_2路选择器_1位_3  (.X0(X[1]), .Out(Out[1]), .Sel(Y[1]), .X1(Sel));
  \_2路选择器_1位  \u_2路选择器_1位_4  (.X0(X[9]), .Out(Out[9]), .Sel(Y[9]), .X1(Sel));
  \_2路选择器_1位  \u_2路选择器_1位_5  (.X0(X[2]), .Out(Out[2]), .Sel(Y[2]), .X1(Sel));
  \_2路选择器_1位  \u_2路选择器_1位_6  (.X0(X[10]), .Out(Out[10]), .Sel(Y[10]), .X1(Sel));
  \_2路选择器_1位  \u_2路选择器_1位_7  (.X0(X[3]), .Out(Out[3]), .Sel(Y[3]), .X1(Sel));
  \_2路选择器_1位  \u_2路选择器_1位_8  (.X0(X[11]), .Out(Out[11]), .Sel(Y[11]), .X1(Sel));
  \_2路选择器_1位  \u_2路选择器_1位_9  (.X0(X[4]), .Out(Out[4]), .Sel(Y[4]), .X1(Sel));
  \_2路选择器_1位  \u_2路选择器_1位_10  (.X0(X[12]), .Out(Out[12]), .Sel(Y[12]), .X1(Sel));
  \_2路选择器_1位  \u_2路选择器_1位_11  (.X0(X[5]), .Out(Out[5]), .Sel(Y[5]), .X1(Sel));
  \_2路选择器_1位  \u_2路选择器_1位_12  (.X0(X[13]), .Out(Out[13]), .Sel(Y[13]), .X1(Sel));
  \_2路选择器_1位  \u_2路选择器_1位_13  (.X0(X[6]), .Out(Out[6]), .Sel(Y[6]), .X1(Sel));
  \_2路选择器_1位  \u_2路选择器_1位_14  (.X0(X[14]), .Out(Out[14]), .Sel(Y[14]), .X1(Sel));
  \_2路选择器_1位  \u_2路选择器_1位_15  (.X0(X[7]), .Out(Out[7]), .Sel(Y[7]), .X1(Sel));
  \_2路选择器_1位  \u_2路选择器_1位_16  (.X0(X[15]), .Out(Out[15]), .Sel(Y[15]), .X1(Sel));
  // Probe on Out
endmodule

module \_2路选择器自动测试  (
);

  wire and_1_out, CLK, comparator_1_eq, d_ff_1_q, d_ff_1_qn, Halt, NEQ, SEL;
  wire [9:0] counter_2_q;
  wire [10:0] counter_1_q;
  wire [15:0] multiplexer_1_out, multiplexer_2_out, multiplexer_2_out_2, \n2路选择器_16位_1_out ;
  wire [31:0] XY;

  Clock clock_1 (.out(CLK));
  Counter #(.width(11), .max('h7ff), .ongoal("stay")) counter_1 (
    .Q(counter_1_q), .carry(Halt), .clk(CLK));  // open: load, D, count, clr
  LED \u_测试完成  (.in(Halt));
  Counter #(.width(10), .max('h3ff)) counter_2 (
    .count(NEQ), .Q(counter_2_q), .clk(CLK), .clr(Halt));  // open: load, D, carry
  and and_1 (and_1_out, ~Halt, NEQ);  // AND_Gate
  ROM #(.addrWidth(11), .dataWidth(32)) rom_1 (.addr(counter_1_q), .data(XY));  // open: sel
  Random #(.width(1)) random_1 (.clk(CLK), .out(SEL));  // open: next, clr
  RAM #(.addrWidth(10), .dataWidth(32), .bus("separate")) ram_1 (
    .addr(counter_2_q), .din(XY), .str(and_1_out), .clk(CLK));  // open: data, sel, ld, clr
  _7_Segment_Display u_7_segment_display_1 (
    .g(multiplexer_2_out[15]), .f(multiplexer_2_out[14]), .a(multiplexer_2_out[13]),
    .b(multiplexer_2_out[12]), .e(multiplexer_2_out_2[15]), .d(multiplexer_2_out_2[14]),
    .c(multiplexer_2_out_2[13]), .dp(multiplexer_2_out_2[12]));
  _7_Segment_Display u_7_segment_display_2 (
    .g(multiplexer_2_out[11]), .f(multiplexer_2_out[10]), .a(multiplexer_2_out[9]), .b(multiplexer_2_out[8]),
    .e(multiplexer_2_out_2[11]), .d(multiplexer_2_out_2[10]), .c(multiplexer_2_out_2[9]),
    .dp(multiplexer_2_out_2[8]));
  D_Flip_Flop d_ff_1 (.clk(CLK), .D(NEQ), .Q(d_ff_1_q), .Qn(d_ff_1_qn), .en(d_ff_1_qn));  // open: preset, reset
  \_2路选择器_16位  \u_2路选择器_16位_1  (.X(XY[15:0]), .Y(XY[31:16]), .Out(\n2路选择器_16位_1_out ), .Sel(SEL));
  _7_Segment_Display u_7_segment_display_3 (
    .g(multiplexer_2_out[7]), .f(multiplexer_2_out[6]), .a(multiplexer_2_out[5]), .b(multiplexer_2_out[4]),
    .e(multiplexer_2_out_2[7]), .d(multiplexer_2_out_2[6]), .c(multiplexer_2_out_2[5]),
    .dp(multiplexer_2_out_2[4]));
  _7_Segment_Display u_7_segment_display_4 (
    .g(multiplexer_2_out[3]), .f(multiplexer_2_out[2]), .a(multiplexer_2_out[1]), .b(multiplexer_2_out[0]),
    .e(multiplexer_2_out_2[3]), .d(multiplexer_2_out_2[2]), .c(multiplexer_2_out_2[1]),
    .dp(multiplexer_2_out_2[0]));
  Multiplexer #(.width(16), .disabled(0), .enable("false")) multiplexer_1 (
    .in0(XY[15:0]), .in1(XY[31:16]), .out(multiplexer_1_out), .sel(SEL));
  Multiplexer #(.width(32), .disabled(0)) multiplexer_2 (
    .in0(32'h8a66ffee), .in1(32'h8a8cef44), .out({multiplexer_2_out_2, multiplexer_2_out}), .sel(d_ff_1_q),
    .en(Halt));
  Comparator #(.width(16)) comparator_1 (
    .a(multiplexer_1_out), .b(\n2路选择器_16位_1_out ), .eq(comparator_1_eq));  // open: gt, lt
  not not_1 (NEQ, comparator_1_eq);

  // Notes on the sheet:
  //   X&Y trace
  //   错误记录X&Y
  //   存储器保存未通过的测试用例
  //   contents of rom_1 (hex, n*v repeats v):
  //   86483f4f 9045b205 fbe9fce5 96280ca8 4899b8c9 4c5a79cc 9b012dbc 9235746a 36687b52 a0441758 f9766af
  //   2bcbc87f ff802acd a0e1645a 5b31cadc 818b2a4a e7335d24 4a5de35 d8a2e906 b9efe7fe 854a3681 3493ad40
  //   480351d2 7627f5e5 bcd68997 3486e006 6cf5520c 413ebb9c 2341bbd8 ea311a86 764210e1 3a307555 faecadbd
  //   18d8f974 20825224 74a6915 d9fde702 ede46977 c6691c8b 9a512ff5 9b7e46e8 6b69326a 7c6a83f0 c33a5362
  //   12a87872 ce72f69d 4edcd791 96da7e5e 2a536aaa f261e612 65567451 1bbd82be e8a40cdb 9db965c1 fee7af6
  //   9571726a bdb68ed5 cae9ead6 bf2aaa6a 79e20ca1 56b3652d d51549ef 1c89dfb 30f5bf34 e9c8517c a980ba5f
  //   8034af9c 8717bc7 d6c1ae9c ae5bcd6f 7064be23 593ca115 f8440ef 2ab79999 49f1178a b72382a c76bca99
  //   15fd59cc fda9c730 840c5a7 6c96a3c1 2e7c0ac 418a8816 8f6def03 2e6a96d5 4ef63fd0 85d39b23 e66733c5
  //   d52340c5 f858303 631c161 c41cfacc 32fe3544 d52c5f84 86439a3e cb793388 49d270b b07748 476ea5cd
  //   2a16cb3f ef7a5417 fed9d034 8ada2b04 1df3364a f6cf75e7 85a09f64 a18a41fe f274d57 fd1375c0 51a48868
  //   89f94237 a648bea6 be3724ea 9a909083 a31d4d3 a8e9534d 610d38f1 740305eb fb4fead9 7fbd4875 d0cdcbe5
  //   cac49b0d 3b72d771 7145fc9b 4669a09c 178df5c7 d98ece2a 647230d1 c8656aec ed4ef2ad 2f300538 3c791dfb
  //   33395bf3 2cdedc46 a325bbaf a6499e14 17b53250 1730d64d e12f63ca d43aa968 2cad0e68 259bbcf1 d22a3128
  //   ba3e67d9 39374aa3 3178b817 31e14b0a b7ad161c 810797ad fd4fc294 2786e297 4fd0fef9 60f79cb7 d5fd6574
  //   e8006d1a f3b0c88f b2915bb5 35b0e737 8994423f 8229558f be73999e c9562f10 732ade5b db3c7a7d 42ac8ab0
  //   e6f29c25 1a3a08a2 c48dc6f3 dfab02aa 9cb010d3 35941d6f bb5aa2df e02a6911 78c571e8 8cb9bc81 bfceffc1
  //   ca81b16d b61fd9e8 bef01b3a 7a6bddef c001978b 8ca3c049 a7423adf 6a48e5d3 e5925fba 321154b8 86b742db
  //   664e5528 ab855b0e 160b4e54 406c3efd 38188041 cd926fa1 c4736eef 57e381b7 490a2743 933de4ce 9143fa51
  //   ecbfea5e 5526df67 b866b375 f4416175 c4464f6e 2fa2d03b 39819a3b bd5361cb f4634cc4 6ea904df b0935c9
  //   c008d876 9997b5e2 22ad9148 cbef5d09 31bd898c d11ec30 a5b4cb81 4b60016d ee0d1b5a 765e5936 644cd8e7
  //   6e9d329 9cb2859e b87d4ce4 d88acf69 9b24e975 fea734cb 40d07fcc 9b30aacf c233aecd 6a49214a b367964
  //   843555f0 6cfe5131 eb831ab5 65ce1a45 a63c07fb 89ccf667 966871b 4408a6f 141c35b1 28e8f435 9259d640
  //   6a13cb84 a86f56a6 2a314ca9 f6f2e8db 816c2f0a 892dbe85 f912ae52 ddc8abd8 7bc6f0aa 30b7ca4a db173885
  //   2bfb2794 409c3474 f63ca186 fc46439a 72e54325 567aa91a 3543cb9f f7d06d2d 7f5f7b90 42130e32 6332d90f
  //   9f08285e de2ecf12 efcdde76 edfc60a1 f86b1213 ffaf1c59 43e95e04 3cb990b8 e0844932 ee7c35c8 6c24c9f
  //   6dc39489 a2b40ae9 3dd0e8b8 f2cd7bec 89f60d5e cc6cd2e7 208738b3 d3ec89b7 2e17dfd2 2e3a3fa1 f5190eb8
  //   d02bfe2d b5fb9518 76e9fa8f b1b49c7b bc9d0e21 94bc9035 5a72e46e 716bb3a3 b1e14149 ce925742 4bbac57c
  //   24b9510b f223c7f cf0730ac 3a1ec1c0 880c9c03 2393f001 adf35475 85a6d141 b6bc998d 724369b2 3271f171
  //   bb107c4a ebbbd3a2 d5d88b58 9919468b 27611bae 7797346b d614e4dd a6130fff b573dcff 18bf5589 ab3df28f
  //   7046889f d2fbcad6 6bcf834f 5844ff61 6c993f0f 91b61910 979b403 d762eb29 a35fff0a 610cf50c 52f2b322
  //   b20214e1 fa6d0e9c 582f19ee 582dc09a e834a8e8 afbcff66 1ca468e0 60eae40f 6999933f 579753de 41abc54d
  //   668f3418 757655cd 10c388e d327525 6cf25180 25f0029c e10c9151 a3f9451e 97c05687 96b19a1a a2ed9a9b
  //   bb7fb0ee ccc37a1f 25f20d5b 10fd5eaf 59914f93 9d5ca730 23b02453 44e13ee7 62d5c38c 46a647d6 21e881d
  //   49cbd0f0 87876f1d 4c30849e 279e3137 a62b500c 83792c90 38fa37ce 824979c4 7345e250 e8d74a70 613dd49c
  //   d2f613cb 934cf1e5 4f940bce 49dd8272 75b82374 8dc4da49 8a33ec7d 13adac32 9c54bd4e 32b2298c 6fb1e957
  //   a591436c 1fb6088d 32d1b593 25780c76 444ef7aa 24574545 7234c559 1fec7d7d 63aa1a6 eec2f6b1 4eee8e2a
  //   fd755ce 8f422290 d4a17170 fb1444e8 aae978d2 73a0f74a d87a0dc3 34250347 f1f0b035 7871bfac 162d3dd1
  //   2602c112 cbc94c28 dd88f9c1 d851c7e5 78f9a165 44e1879e 5f783109 5f0364ab fce6d3f1 8426f091 674ce1b7
  //   b3550178 eb644a3d d37a143b db924ff1 3b7ce680 6bf280e0 7748af5f 6f519314 46f5011e 336d9cc9 42b2a27f
  //   943f14ee db2d9211 57af1c78 dfa1ea24 10f8c503 4d147fbb 95115d43 e881db1a 9f2c3fca 8d978c61 619e3494
  //   b7c5e2b2 13b029ee a36bb06f 9505dd26 fc340b00 e00fff8e fec7d8b1 b90f784c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
  //   多路选择器自动测试
  //   ctrl+K驱动时钟自动测试
endmodule

// 4位数比较器
module \_4位无符号比较器  (
  input  X3,
  input  X2,
  input  X1,
  input  X0,
  input  Y3,
  input  Y2,
  input  Y1,
  input  Y0,
  output Great,
  output Equal,
  output Less
);

  wire and_1_out, and_2_out, and_3_out, and_4_out, and_5_out, and_6_out, not_1_out, not_2_out, not_3_out,
       not_4_out, or_1_out, or_2_out, xnor_1_out, xnor_2_out, xnor_3_out, xor_1_out, xor_2_out, xor_3_out,
       xor_4_out;

  not not_1 (not_1_out, Y1);
  not not_2 (not_2_out, Y0);
  xnor xnor_1 (xnor_1_out, X1, Y1);
  xor xor_1 (xor_1_out, X3, Y3);
  xor xor_2 (xor_2_out, X2, Y2);
  xor xor_3 (xor_3_out, X1, Y1);
  xor xor_4 (xor_4_out, X0, Y0);
  and and_1 (and_1_out, X1, not_1_out);
  and and_2 (and_2_out, X0, not_2_out, xnor_1_out);
  nor nor_1 (Equal, xor_1_out, xor_2_out, xor_3_out, xor_4_out);
  not not_3 (not_3_out, Y2);
  xnor xnor_2 (xnor_2_out, X2, Y2);
  or or_1 (or_1_out, and_1_out, and_2_out);
  not not_4 (not_4_out, Y3);
  xnor xnor_3 (xnor_3_out, X3, Y3);
  and and_3 (and_3_out, X2, not_3_out);
  or or_2 (or_2_out, and_3_out, and_4_out);
  and and_4 (and_4_out, xnor_2_out, or_1_out);
  and and_5 (and_5_out, X3, not_4_out);
  and and_6 (and_6_out, xnor_3_out, or_2_out);
  or or_3 (Great, and_5_out, and_6_out);
  xnor xnor_4 (Less, Great, Equal);
endmodule

module \_16位无符号比较器  (
  input  [15:0] X,
  input  [15:0] Y,
  output Great,
  output Equal,
  output Less
);

  wire \n4位无符号比较器_1_equal , \n4位无符号比较器_1_great , \n4位无符号比较器_1_less , \n4位无符号比较器_2_equal ,
       \n4位无符号比较器_2_great , \n4位无符号比较器_2_less , \n4位无符号比较器_3_equal , \n4位无符号比较器_3_great , \n4位无符号比较器_3_less ,
       \n4位无符号比较器_4_equal , \n4位无符号比较器_4_great , \n4位无符号比较器_4_less , xor_1_out, xor_2_out, xor_3_out,
       xor_4_out, xor_5_out, xor_6_out, xor_7_out, xor_8_out;

  // Probe on X
  // Probe on Y
  \_4位无符号比较器  \u_4位无符号比较器_1  (
    .X3(X[15]), .X2(X[14]), .X1(X[13]), .X0(X[12]), .Y3(Y[15]), .Y2(Y[14]), .Y1(Y[13]), .Y0(Y[12]),
    .Great(\n4位无符号比较器_1_great ), .Equal(\n4位无符号比较器_1_equal ), .Less(\n4位无符号比较器_1_less ));
  \_4位无符号比较器  \u_4位无符号比较器_2  (
    .X3(X[11]), .X2(X[10]), .X1(X[9]), .X0(X[8]), .Y3(Y[11]), .Y2(Y[10]), .Y1(Y[9]), .Y0(Y[8]),
    .Great(\n4位无符号比较器_2_great ), .Equal(\n4位无符号比较器_2_equal ), .Less(\n4位无符号比较器_2_less ));
  \_4位无符号比较器  \u_4位无符号比较器_3  (
    .X3(X[7]), .X2(X[6]), .X1(X[5]), .X0(X[4]), .Y3(Y[7]), .Y2(Y[6]), .Y1(Y[5]), .Y0(Y[4]),
    .Great(\n4位无符号比较器_3_great ), .Equal(\n4位无符号比较器_3_equal ), .Less(\n4位无符号比较器_3_less ));
  \_4位无符号比较器  \u_4位无符号比较器_4  (
    .X3(X[3]), .X2(X[2]), .X1(X[1]), .X0(X[0]), .Y3(Y[3]), .Y2(Y[2]), .Y1(Y[1]), .Y0(Y[0]),
    .Great(\n4位无符号比较器_4_great ), .Equal(\n4位无符号比较器_4_equal ), .Less(\n4位无符号比较器_4_less ));
  xor xor_1 (xor_1_out, \n4位无符号比较器_1_great , \n4位无符号比较器_1_equal );
  xor xor_2 (xor_2_out, \n4位无符号比较器_1_equal , \n4位无符号比较器_1_less );
  xor xor_3 (xor_3_out, \n4位无符号比较器_2_great , \n4位无符号比较器_2_equal );
  xor xor_4 (xor_4_out, \n4位无符号比较器_2_equal , \n4位无符号比较器_2_less );
  xor xor_5 (xor_5_out, \n4位无符号比较器_3_great , \n4位无符号比较器_3_equal );
  xor xor_6 (xor_6_out, \n4位无符号比较器_3_equal , \n4位无符号比较器_3_less );
  xor xor_7 (xor_7_out, \n4位无符号比较器_4_great , \n4位无符号比较器_4_equal );
  xor xor_8 (xor_8_out, \n4位无符号比较器_4_equal , \n4位无符号比较器_4_less );
  \_4位无符号比较器  \u_4位无符号比较器_5  (
    .X3(xor_1_out), .X2(xor_3_out), .X1(xor_5_out), .X0(xor_7_out), .Y3(xor_2_out), .Y2(xor_4_out),
    .Y1(xor_6_out), .Y0(xor_8_out), .Great(Great), .Equal(Equal), .Less(Less));

  // Other names for the same wires on the sheet: X0[3:0] = X[3:0]; X1[3:0] = X[7:4]; X2[3:0] = X[11:8];
  //   X3[3:0] = X[15:12]; Y0[3:0] = Y[3:0]; Y1[3:0] = Y[7:4]; Y2[3:0] = Y[11:8]; Y3[3:0] = Y[15:12]

  // Notes on the sheet:
  //   电路功能：X,Y进行无符号比较，Great=(X>Y)?1:0;
  //   输入引脚区
  //   输出引脚区
endmodule

// 16位2-1 MUX
module \_16位无符号比较器自动测试  (
);

  wire and_1_out, CLK, comparator_2_eq, d_ff_1_q, d_ff_1_qn, Halt, NEQ;
  wire [2:0] comparator_1_gt, \n16位无符号比较器_1_great ;
  wire [7:0] counter_1_q;
  wire [9:0] counter_2_q;
  wire [15:0] multiplexer_1_out, multiplexer_1_out_2;
  wire [31:0] XY;

  Counter #(.ongoal("stay")) counter_1 (.Q(counter_1_q), .carry(Halt), .clk(CLK));  // open: load, D, count, clr
  Counter #(.width(10), .max('h3ff)) counter_2 (
    .count(NEQ), .Q(counter_2_q), .clk(CLK), .clr(Halt));  // open: load, D, carry
  LED \u_测试完成  (.in(Halt));
  and and_1 (and_1_out, ~Halt, NEQ);  // AND_Gate
  Clock clock_1 (.out(CLK));
  ROM #(.dataWidth(32)) rom_1 (.addr(counter_1_q), .data(XY));  // open: sel
  RAM #(.addrWidth(10), .dataWidth(32), .bus("separate")) ram_1 (
    .addr(counter_2_q), .din(XY), .str(and_1_out), .clk(CLK));  // open: data, sel, ld, clr
  _7_Segment_Display u_7_segment_display_1 (
    .g(multiplexer_1_out[11]), .f(multiplexer_1_out[10]), .a(multiplexer_1_out[9]), .b(multiplexer_1_out[8]),
    .e(multiplexer_1_out_2[11]), .d(multiplexer_1_out_2[10]), .c(multiplexer_1_out_2[9]),
    .dp(multiplexer_1_out_2[8]));
  _7_Segment_Display u_7_segment_display_2 (
    .g(multiplexer_1_out[15]), .f(multiplexer_1_out[14]), .a(multiplexer_1_out[13]),
    .b(multiplexer_1_out[12]), .e(multiplexer_1_out_2[15]), .d(multiplexer_1_out_2[14]),
    .c(multiplexer_1_out_2[13]), .dp(multiplexer_1_out_2[12]));
  D_Flip_Flop d_ff_1 (.clk(CLK), .D(NEQ), .Q(d_ff_1_q), .Qn(d_ff_1_qn), .en(d_ff_1_qn));  // open: preset, reset
  \_16位无符号比较器  \u_16位无符号比较器_1  (
    .X(XY[15:0]), .Y(XY[31:16]), .Great(\n16位无符号比较器_1_great [0]), .Equal(\n16位无符号比较器_1_great [1]),
    .Less(\n16位无符号比较器_1_great [2]));
  Comparator #(.width(16), .mode("unsigned")) comparator_1 (
    .a(XY[15:0]), .b(XY[31:16]), .gt(comparator_1_gt[0]), .eq(comparator_1_gt[1]), .lt(comparator_1_gt[2]));
  _7_Segment_Display u_7_segment_display_3 (
    .g(multiplexer_1_out[7]), .f(multiplexer_1_out[6]), .a(multiplexer_1_out[5]), .b(multiplexer_1_out[4]),
    .e(multiplexer_1_out_2[7]), .d(multiplexer_1_out_2[6]), .c(multiplexer_1_out_2[5]),
    .dp(multiplexer_1_out_2[4]));
  _7_Segment_Display u_7_segment_display_4 (
    .g(multiplexer_1_out[3]), .f(multiplexer_1_out[2]), .a(multiplexer_1_out[1]), .b(multiplexer_1_out[0]),
    .e(multiplexer_1_out_2[3]), .d(multiplexer_1_out_2[2]), .c(multiplexer_1_out_2[1]),
    .dp(multiplexer_1_out_2[0]));
  not not_1 (NEQ, comparator_2_eq);
  Comparator #(.width(3)) comparator_2 (
    .a(\n16位无符号比较器_1_great ), .b(comparator_1_gt), .eq(comparator_2_eq));  // open: gt, lt
  Multiplexer #(.width(32), .disabled(0)) multiplexer_1 (
    .in0(32'h8a66ffee), .in1(32'h8a8cef44), .out({multiplexer_1_out_2, multiplexer_1_out}), .sel(d_ff_1_q),
    .en(Halt));

  // Notes on the sheet:
  //   X&Y trace
  //   错误记录X&Y
  //   存储器保存未通过的测试用例
  //   contents of rom_1 (hex, n*v repeats v):
  //   ffffffff ffff7fff ffffbfff ffffdfff ffffefff f7fff7ff fffff7ff fffffbff fffffdff fffffeff ff7fff7f
  //   ff7fff7f ffffff7f ffffffbf ffffffdf ffffffef fff7fff7 fffffff7 fffffffb fffffffd fffffffe 0 1 2 4 8
  //   100010 10 20 40 80 1000100 100 200 400 800 10001000 1000 2000 4000 8000 f4815766 588f50e1 691a47b9
  //   953cad65 f4d07a42 847bfafc 699a478c d3a3b941 45a67aa3 40ad61ed fbdbd7af ad681465 6d29551b f8b4a89f
  //   c46931ce 6da641d0 a32356fb c8596d72 c8d957f6 a225ef12 e2f0e69e dac18d78 2c29b6da e8498992 849a8fa0
  //   cc89dbb9 96e7ac10 d859e7c7 ed1b931f 9a6b0c71 5dc43051 905b4680 fd993c02 dc7a144e e08fe5be 3d2cda1d
  //   3953372f b7c73bb4 9541ca16 a38833d4 66592fd4 11325f9 a28ecd02 2689baee 3995efa0 b7850caa f7bc8a4b
  //   72bf7a08 2f844308 b9c16ec6 d7bd681f 5f4f8054 be5e184 167473ff 78485951 969b16d7 e01899d1 8f5743fd
  //   86828397 40d809aa 6d2a022d 6eb919b 3df509cb 916d453a 8dec9f 119c9a28 a7ed3a2b 4f740789 8c5fdf2d
  //   76a8d8a9 3509609a e92e56c fa5bd025 82bad13 14987cde e37be3cc 173e6657 fd23792 99971ce1 42aae4e6
  //   b700fd56 133aa7c6 7779af1 fc95a98b dd69adbb 9bb14002 ed880001 c452a662 dab9962 ecf24c8d aaabc9e7
  //   70cfed22 eb57bbac 61cc4ee1 f043d59d 890769da d2a27dbd eff19cf0 8682ad82 3d31b42a 2064ebd d1fcb45b
  //   d20f7b97 85ccb489 9f8f8018 7b9e81b9 8ebddfc3 d15f5d7e d4a1a5be fc21dbd8 144ea10 c737b8e8 2fcaba65
  //   42e372f4 ee4378ec c3f48937 793c47c3 c117402 93843b6a a87fbeb1 6fc6d2d5 85fa1fea 95579780 713300af
  //   fdb7cc1c 346496c5 70fdb449 25338adf 22be43dc abe31724 f27ee841 99a69e81 15fea25d 26c1f149 bf4cb8c
  //   1533c7ab 45c1a42b a42a6e6d 222a2e30 2a5e3686 5caeda57 c02aab14 765acad5 4706d961 fe025b53 922c42e5
  //   b89287ec 70e6f79d 60622e31 d91c7840 cd0cd37 b1c0a92e 4b6f62a6 b10aebaf f62577cd 73fa0e0d aca68551
  //   f99276ec 233c77e6 c9cfc487 eac76497 39b70c27 19695f22 460dfa7d d920e8e0 367a4942 d3592c2 c4c152a6
  //   efda30d8 245dff15 6b7761ed 8b08ddc9 c54931b0 603fecac 181c3fed e6866805 8d2b1b5b 2f6dee84 68346271
  //   777e5a0b 7396c0d3 dd85e1d3 ff7203cb 688c6e5f 46c54453 9ca87bbe e2328930 17e67a9c 9051479b 5ba54a2
  //   604bccfb 747a8cad c050e030 6ee2674d 5e3bcceb 20c99c16 66b28f9a 3a294443 95fcfc62 22340f2a ed897fa6
  //   b11038fb 92a57aa5 91815453 5d7942a2 302bab20 8e1b6d1f bcbfcf4f 303557a5 c33fe7d1 5a8cbd9f 72e5a6e
  //   180cb2c6 9313a6e2 c5fc7c97
  //   16位数无符号比较器自动测试
  //   ctrl+K驱动时钟自动测试
endmodule

// 4位寄存器
module \_4位并行加载寄存器  (
  input  CLK,
  input  [3:0] Din,
  input  \使能_高电平有效 ,
  output [3:0] \输出Q 
);

  D_Flip_Flop d_ff_1 (.clk(CLK), .D(Din[0]), .Q(\输出Q [0]), .en(\使能_高电平有效 ));  // open: Qn, preset, reset
  D_Flip_Flop d_ff_2 (.clk(CLK), .D(Din[1]), .Q(\输出Q [1]), .en(\使能_高电平有效 ));  // open: Qn, preset, reset
  D_Flip_Flop d_ff_3 (.clk(CLK), .D(Din[2]), .Q(\输出Q [2]), .en(\使能_高电平有效 ));  // open: Qn, preset, reset
  D_Flip_Flop d_ff_4 (.clk(CLK), .D(Din[3]), .Q(\输出Q [3]), .en(\使能_高电平有效 ));  // open: Qn, preset, reset
  // Probe on \输出Q 

  // Other names for the same wires on the sheet: En = \使能_高电平有效 ; Q[3:0] = \输出Q 

  // Notes on the sheet:
  //   输入引脚区
  //   4位并行加载寄存器，输入Din 4位；输出Q 4位；En：使能端；
  //   请勿增删改引脚，请在下方利用上方输入输出引脚的隧道标签信号构建电路，ctrl+d复制选择组件
  //   输出引脚区
endmodule

// 16位寄存器 SD
module \_16位并行加载寄存器  (
  input  CLK,
  input  [15:0] Din,
  input  \使能_高电平有效 ,
  output [15:0] \输出Q 
);

  // Probe on Din
  \_4位并行加载寄存器  \u_4位并行加载寄存器_1  (.Din(Din[3:0]), .\输出Q (\输出Q [3:0]), .CLK(CLK), .\使能_高电平有效 (\使能_高电平有效 ));
  \_4位并行加载寄存器  \u_4位并行加载寄存器_2  (.Din(Din[7:4]), .\输出Q (\输出Q [7:4]), .CLK(CLK), .\使能_高电平有效 (\使能_高电平有效 ));
  \_4位并行加载寄存器  \u_4位并行加载寄存器_3  (.Din(Din[11:8]), .\输出Q (\输出Q [11:8]), .CLK(CLK), .\使能_高电平有效 (\使能_高电平有效 ));
  \_4位并行加载寄存器  \u_4位并行加载寄存器_4  (.Din(Din[15:12]), .\输出Q (\输出Q [15:12]), .CLK(CLK), .\使能_高电平有效 (\使能_高电平有效 ));
  // Probe on \输出Q 

  // Other names for the same wires on the sheet: En = \使能_高电平有效 ; Q[15:0] = \输出Q 

  // Notes on the sheet:
  //   输入引脚区
  //   16位并行加载寄存器，输入Din 16位；输出Q 16位；En：使能端；
  //   请勿增删改引脚，请在下方利用上方输入输出引脚的隧道标签信号构建电路，ctrl+d复制选择组件
  //   输出引脚区
endmodule

module \_4位BCD计数器  (
  input  CLK,
  input  \使能_高电平有效 ,
  input  \异步复位_高电平有效 ,
  output [3:0] \输出Q ,
  output \进位输出 
);

  wire \bcd计数器状态转换_自动生成_1_n0 , \bcd计数器状态转换_自动生成_1_n1 , \bcd计数器状态转换_自动生成_1_n2 , \bcd计数器状态转换_自动生成_1_n3 ;

  \BCD计数器状态转换_自动生成  \bcd计数器状态转换_自动生成_1  (
    .S3(\输出Q [3]), .S2(\输出Q [2]), .N3(\bcd计数器状态转换_自动生成_1_n3 ), .S1(\输出Q [1]), .S0(\输出Q [0]),
    .N2(\bcd计数器状态转换_自动生成_1_n2 ), .N1(\bcd计数器状态转换_自动生成_1_n1 ), .N0(\bcd计数器状态转换_自动生成_1_n0 ));
  \BCD计数器输出函数_自动生成  \bcd计数器输出函数_自动生成_1  (.S3(\输出Q [3]), .Cout(\进位输出 ), .S2(\输出Q [2]), .S1(\输出Q [1]), .S0(\输出Q [0]));
  // Probe on \输出Q 
  D_Flip_Flop d_ff_1 (
    .clk(CLK), .D(\bcd计数器状态转换_自动生成_1_n3 ), .Q(\输出Q [3]), .en(\使能_高电平有效 ), .reset(\异步复位_高电平有效 ));  // open: Qn, preset
  D_Flip_Flop d_ff_2 (
    .clk(CLK), .D(\bcd计数器状态转换_自动生成_1_n2 ), .Q(\输出Q [2]), .en(\使能_高电平有效 ), .reset(\异步复位_高电平有效 ));  // open: Qn, preset
  D_Flip_Flop d_ff_3 (
    .clk(CLK), .D(\bcd计数器状态转换_自动生成_1_n1 ), .Q(\输出Q [1]), .en(\使能_高电平有效 ), .reset(\异步复位_高电平有效 ));  // open: Qn, preset
  D_Flip_Flop d_ff_4 (
    .clk(CLK), .D(\bcd计数器状态转换_自动生成_1_n0 ), .Q(\输出Q [0]), .en(\使能_高电平有效 ), .reset(\异步复位_高电平有效 ));  // open: Qn, preset

  // Other names for the same wires on the sheet: Cout = \进位输出 ; En = \使能_高电平有效 ; Q[3:0] = \输出Q ; Rst = \异步复位_高电平有效 

  // Notes on the sheet:
  //   输入引脚区
  //   4位BCD(1位十进制)计数器，输出Q在0-9之间循环计数，EN使能端；Rst异步复位；Cout=(Q==9)?1:0;
  //   请勿增删改引脚，请在下方利用上方输入输出引脚的隧道标签信号构建电路，ctrl+d复制选择组件
  //   输出引脚区
endmodule

// 状态转换
module \BCD计数器状态转换_自动生成  (
  input  S3,
  input  S2,
  input  S1,
  input  S0,
  output N3,
  output N2,
  output N1,
  output N0
);

  wire and_1_out, and_2_out, and_3_out, and_4_out, and_5_out, and_6_out, and_7_out, and_8_out, and_9_out,
       and_10_out, and_11_out, and_12_out, and_13_out, and_14_out, and_15_out, not_1_out, not_2_out,
       not_3_out, not_4_out, not_5_out, not_6_out, not_7_out, not_8_out, not_9_out, not_10_out, not_11_out,
       not_12_out, not_13_out, not_14_out, not_15_out, not_16_out, not_17_out, not_18_out, not_19_out,
       not_20_out, not_21_out, not_22_out, not_23_out, not_24_out, not_25_out, not_26_out, not_27_out,
       not_28_out, not_29_out, not_30_out, not_31_out, not_32_out, not_33_out, not_34_out, not_35_out,
       not_36_out, not_37_out, not_38_out;

  not not_1 (not_1_out, S3);
  not not_2 (not_2_out, S2);
  not not_3 (not_3_out, S1);
  not not_4 (not_4_out, S0);
  not not_5 (not_5_out, S3);
  not not_6 (not_6_out, S2);
  not not_7 (not_7_out, S3);
  not not_8 (not_8_out, S1);
  not not_9 (not_9_out, S0);
  not not_10 (not_10_out, S3);
  not not_11 (not_11_out, S1);
  not not_12 (not_12_out, S3);
  not not_13 (not_13_out, S0);
  not not_14 (not_14_out, S3);
  not not_15 (not_15_out, S2);
  not not_16 (not_16_out, S1);
  not not_17 (not_17_out, S3);
  not not_18 (not_18_out, S2);
  not not_19 (not_19_out, S0);
  not not_20 (not_20_out, S3);
  not not_21 (not_21_out, S1);
  not not_22 (not_22_out, S3);
  not not_23 (not_23_out, S0);
  not not_24 (not_24_out, S3);
  not not_25 (not_25_out, S2);
  not not_26 (not_26_out, S1);
  not not_27 (not_27_out, S0);
  not not_28 (not_28_out, S3);
  not not_29 (not_29_out, S2);
  not not_30 (not_30_out, S0);
  not not_31 (not_31_out, S3);
  not not_32 (not_32_out, S1);
  not not_33 (not_33_out, S0);
  not not_34 (not_34_out, S3);
  not not_35 (not_35_out, S0);
  not not_36 (not_36_out, S2);
  not not_37 (not_37_out, S1);
  not not_38 (not_38_out, S0);
  and and_1 (and_1_out, not_1_out, S2, S1, S0);
  or or_1 (N3, and_1_out, and_2_out);
  and and_2 (and_2_out, S3, not_2_out, not_3_out, not_4_out);
  and and_3 (and_3_out, not_5_out, not_6_out, S1, S0);
  and and_4 (and_4_out, not_7_out, S2, not_8_out, not_9_out);
  and and_5 (and_5_out, not_10_out, S2, not_11_out, S0);
  and and_6 (and_6_out, not_12_out, S2, S1, not_13_out);
  and and_7 (and_7_out, not_14_out, not_15_out, not_16_out, S0);
  and and_8 (and_8_out, not_17_out, not_18_out, S1, not_19_out);
  and and_9 (and_9_out, not_20_out, S2, not_21_out, S0);
  and and_10 (and_10_out, not_22_out, S2, S1, not_23_out);
  and and_11 (and_11_out, not_24_out, not_25_out, not_26_out, not_27_out);
  and and_12 (and_12_out, not_28_out, not_29_out, S1, not_30_out);
  and and_13 (and_13_out, not_31_out, S2, not_32_out, not_33_out);
  and and_14 (and_14_out, not_34_out, S2, S1, not_35_out);
  and and_15 (and_15_out, S3, not_36_out, not_37_out, not_38_out);
  or or_2 (N2, and_3_out, and_4_out, and_5_out, and_6_out);
  or or_3 (N1, and_7_out, and_8_out, and_9_out, and_10_out);
  or or_4 (N0, and_11_out, and_12_out, and_13_out, and_14_out, and_15_out);
endmodule

module \BCD计数器输出函数_自动生成  (
  input  S3,
  input  S2,
  input  S1,
  input  S0,
  output Cout
);

  wire not_1_out;

  and and_1 (Cout, S3, not_1_out, S0);
  not not_1 (not_1_out, S1);
endmodule

// 计时器 TM
module \码表计数器  (
  input  CLK,
  input  En,
  input  Rst,
  output [15:0] \输出Q 
);

  wire and_1_out, and_2_out, \n4位bcd计数器_2_进位输出 , \n4位bcd计数器_3_进位输出 , \n4位bcd计数器_4_进位输出 ;

  \_4位BCD计数器  \u_4位bcd计数器_1  (
    .CLK(CLK), .\异步复位_高电平有效 (Rst), .\使能_高电平有效 (and_1_out), .\输出Q (\输出Q [15:12]));  // open: 进位输出
  and and_1 (and_1_out, and_2_out, \n4位bcd计数器_2_进位输出 );
  // Probe on \输出Q 
  \_4位BCD计数器  \u_4位bcd计数器_2  (
    .CLK(CLK), .\异步复位_高电平有效 (Rst), .\使能_高电平有效 (and_2_out), .\输出Q (\输出Q [11:8]), .\进位输出 (\n4位bcd计数器_2_进位输出 ));
  and and_2 (and_2_out, \n4位bcd计数器_4_进位输出 , \n4位bcd计数器_3_进位输出 );
  \_4位BCD计数器  \u_4位bcd计数器_3  (
    .CLK(CLK), .\异步复位_高电平有效 (Rst), .\使能_高电平有效 (\n4位bcd计数器_4_进位输出 ), .\输出Q (\输出Q [7:4]),
    .\进位输出 (\n4位bcd计数器_3_进位输出 ));
  \_4位BCD计数器  \u_4位bcd计数器_4  (
    .CLK(CLK), .\异步复位_高电平有效 (Rst), .\使能_高电平有效 (En), .\输出Q (\输出Q [3:0]), .\进位输出 (\n4位bcd计数器_4_进位输出 ));

  // Other names for the same wires on the sheet: Q[15:0] = \输出Q 

  // Notes on the sheet:
  //   输入引脚区
  //   码表计数器，16位输出，包括4个BCD计数器，分别对应10秒、1秒、1/10秒、1/100秒。
  //   低位计数到9时，相邻高位在时钟到来时加1。                    En：使能端；Rst：异步复位；
  //   输出引脚区
endmodule

module \码表计数器自动测试  (
  input  Rst
);

  wire CLK_out;
  wire [3:0] \码表计数器_1_输出q_2 , \码表计数器_1_输出q_3 ;
  wire [7:0] \码表计数器_1_输出q ;

  Hex_Digit_Display hex_digit_display_1 (.value(\码表计数器_1_输出q_2 ), .dp(1'b1));
  Hex_Digit_Display hex_digit_display_2 (.value(\码表计数器_1_输出q_3 ));  // open: dp
  \码表计数器  \u_码表计数器_1  (.CLK(CLK_out), .En(1'b1), .Rst(Rst), .\输出Q ({\码表计数器_1_输出q_3 , \码表计数器_1_输出q_2 , \码表计数器_1_输出q }));
  Hex_Digit_Display hex_digit_display_3 (.value(\码表计数器_1_输出q [3:0]));  // open: dp
  Hex_Digit_Display hex_digit_display_4 (.value(\码表计数器_1_输出q [7:4]));  // open: dp
  Clock CLK (.out(CLK_out));

  // Notes on the sheet:
  //   En
  //   Ctrl+K驱动时钟自动测试
endmodule

// 码表显示 DP
module \码表显示驱动  (
  input  [15:0] _16bitDin,
  output [31:0] \数码管显示控制 
);

  \数码管驱动  \u_数码管驱动_1  (
    .X3(_16bitDin[15]), .X2(_16bitDin[14]), .Seg_1(\数码管显示控制 [31]), .X1(_16bitDin[13]), .X0(_16bitDin[12]),
    .Seg_2(\数码管显示控制 [30]), .Seg_3(\数码管显示控制 [29]), .Seg_4(\数码管显示控制 [28]), .Seg_5(\数码管显示控制 [27]),
    .Seg_6(\数码管显示控制 [26]), .Seg_7(\数码管显示控制 [25]));
  \数码管驱动  \u_数码管驱动_2  (
    .X3(_16bitDin[11]), .X2(_16bitDin[10]), .Seg_1(\数码管显示控制 [23]), .X1(_16bitDin[9]), .X0(_16bitDin[8]),
    .Seg_2(\数码管显示控制 [22]), .Seg_3(\数码管显示控制 [21]), .Seg_4(\数码管显示控制 [20]), .Seg_5(\数码管显示控制 [19]),
    .Seg_6(\数码管显示控制 [18]), .Seg_7(\数码管显示控制 [17]));
  \数码管驱动  \u_数码管驱动_3  (
    .X3(_16bitDin[7]), .X2(_16bitDin[6]), .Seg_1(\数码管显示控制 [15]), .X1(_16bitDin[5]), .X0(_16bitDin[4]),
    .Seg_2(\数码管显示控制 [14]), .Seg_3(\数码管显示控制 [13]), .Seg_4(\数码管显示控制 [12]), .Seg_5(\数码管显示控制 [11]),
    .Seg_6(\数码管显示控制 [10]), .Seg_7(\数码管显示控制 [9]));
  \数码管驱动  \u_数码管驱动_4  (
    .X3(_16bitDin[3]), .X2(_16bitDin[2]), .Seg_1(\数码管显示控制 [7]), .X1(_16bitDin[1]), .X0(_16bitDin[0]),
    .Seg_2(\数码管显示控制 [6]), .Seg_3(\数码管显示控制 [5]), .Seg_4(\数码管显示控制 [4]), .Seg_5(\数码管显示控制 [3]),
    .Seg_6(\数码管显示控制 [2]), .Seg_7(\数码管显示控制 [1]));

  assign {\数码管显示控制 [24], \数码管显示控制 [16], \数码管显示控制 [8], \数码管显示控制 [0]} = 4'b0100;

  // Other names for the same wires on the sheet: Din[15:0] = _16bitDin;
  //   DispInfo (some bits) = {\数码管显示控制 [31:25], \数码管显示控制 [23:17], \数码管显示控制 [15:9], \数码管显示控制 [7:1]}

  // Notes on the sheet:
  //   输入引脚区
  //   码表计数显示输出驱动，将16位BCD数据输出到四个7段数码管，输出为4个数码管的控制信息，共32位。
  //   输出引脚区
endmodule

module \码表控制器  (
  input  start,
  input  stop,
  input  store,
  input  reset,
  input  NewRecord,
  input  CLK,
  output SDsel,
  output SDen,
  output DP_Sel,
  output TMen,
  output TMreset
);

  \码表控制器状态转换_自动生成  \u_码表控制器状态转换_自动生成_1  ();  // open: start, stop, store, reset, NewRecord, S2, S1, S0, N2, N1, N0
  D_Flip_Flop d_ff_1 ();  // open: clk, D, Q, Qn, preset, en, reset
  D_Flip_Flop d_ff_2 ();  // open: clk, D, Q, Qn, preset, en, reset
  D_Flip_Flop d_ff_3 ();  // open: clk, D, Q, Qn, preset, en, reset
  \码表控制器输出函数_自动生成  \u_码表控制器输出函数_自动生成_1  (
    .SDSel(SDsel), .SDEN(SDen), .DPSEL(DP_Sel), .TMSel(TMen), .TMReset(TMreset));  // open: S2, S1, S0
endmodule

// 状态转换
module \码表控制器状态转换_自动生成  (
  input  start,
  input  stop,
  input  store,
  input  reset,
  input  NewRecord,
  input  S2,
  input  S1,
  input  S0,
  output N2,
  output N1,
  output N0
);
endmodule

// 输出函数
module \码表控制器输出函数_自动生成  (
  input  S2,
  input  S1,
  input  S0,
  output SDSel,
  output SDEN,
  output DPSEL,
  output TMSel,
  output TMReset
);
endmodule

module \运动码表  (
  input  eduStart,
  input  eduStop,
  input  eduStore,
  input  eduReset,
  input  eduCLK,
  input  TestMode,
  output [15:0] Time
);

  wire CLK, CLK_out, DP_SEL, NewRecord, Reset, Reset1, SD_EN, SD_SEL, Start, Start1, Stop, Stop1, Store,
       Store1, TM_EN, TM_Reset;
  wire [15:0] \n16位并行加载寄存器_1_输出q ;
  wire [31:0] DispInfo;

  Button u_Start (.out(Start));
  Button u_Stop (.out(Stop));
  Button u_Store (.out(Store));
  Button u_Reset (.out(Reset));
  Multiplexer #(.enable("false")) multiplexer_1 (.in0(Start), .in1(eduStart), .out(Start1), .sel(TestMode));
  _7_Segment_Display u_7_segment_display_1 (
    .g(DispInfo[28]), .f(DispInfo[29]), .a(DispInfo[30]), .b(DispInfo[31]), .e(DispInfo[24]),
    .d(DispInfo[25]), .c(DispInfo[26]), .dp(DispInfo[27]));
  _7_Segment_Display u_7_segment_display_2 (
    .g(DispInfo[20]), .f(DispInfo[21]), .a(DispInfo[22]), .b(DispInfo[23]), .e(DispInfo[16]),
    .d(DispInfo[17]), .c(DispInfo[18]), .dp(DispInfo[19]));
  _7_Segment_Display u_7_segment_display_3 (
    .g(DispInfo[12]), .f(DispInfo[13]), .a(DispInfo[14]), .b(DispInfo[15]), .e(DispInfo[8]), .d(DispInfo[9]),
    .c(DispInfo[10]), .dp(DispInfo[11]));
  _7_Segment_Display u_7_segment_display_4 (
    .g(DispInfo[4]), .f(DispInfo[5]), .a(DispInfo[6]), .b(DispInfo[7]), .e(DispInfo[0]), .d(DispInfo[1]),
    .c(DispInfo[2]), .dp(DispInfo[3]));
  Multiplexer #(.enable("false")) multiplexer_2 (.in0(Stop), .in1(eduStop), .out(Stop1), .sel(TestMode));
  \_2路选择器_16位  \u_2路选择器_16位_1  (.X(16'h9999));  // open: Y, Out, Sel
  \码表显示驱动  \u_码表显示驱动_1  (._16bitDin(Time), .\数码管显示控制 (DispInfo));
  \_2路选择器_16位  \u_2路选择器_16位_2  (.X(\n16位并行加载寄存器_1_输出q ));  // open: Y, Out, Sel
  \_16位并行加载寄存器  \u_16位并行加载寄存器_1  (.\输出Q (\n16位并行加载寄存器_1_输出q ));  // open: CLK, 使能_高电平有效, Din
  Multiplexer #(.enable("false")) multiplexer_3 (.in0(Store), .in1(eduStore), .out(Store1), .sel(TestMode));
  \码表计数器  \u_码表计数器_1  ();  // open: CLK, En, Rst, 输出Q
  Multiplexer #(.enable("false")) multiplexer_4 (.in0(Reset), .in1(eduReset), .out(Reset1), .sel(TestMode));
  // Probe on nothing
  \_16位无符号比较器  \u_16位无符号比较器_1  (.Great(NewRecord));  // open: X, Y, Equal, Less
  \码表控制器  \u_码表控制器_1  (
    .start(Start1), .stop(Stop1), .store(Store1), .reset(Reset1), .CLK(CLK), .SDsel(SD_SEL), .SDen(SD_EN),
    .DP_Sel(DP_SEL), .TMen(TM_EN), .TMreset(TM_Reset), .NewRecord(NewRecord));
  Clock u_CLK (.out(CLK_out));
  Multiplexer #(.enable("false")) multiplexer_5 (.in0(CLK_out), .in1(eduCLK), .out(CLK), .sel(TestMode));

  // Other names for the same wires on the sheet: S1B[3:0] = DispInfo[3:0]; S1T[3:0] = DispInfo[7:4];
  //   S2B[3:0] = DispInfo[11:8]; S2T[3:0] = DispInfo[15:12]; S3B[3:0] = DispInfo[19:16]; S3T[3:0] = DispInfo[23:20];
  //   S4B[3:0] = DispInfo[27:24]; S4T[3:0] = DispInfo[31:28]

  // Notes on the sheet:
  //   控
  //   制
  //   信
  //   号
  //   TestMode：测试模式控制：0本地测试，1在线测试
  //   运
  //   动
  //   码
  //   表
endmodule
